# Fritzing sketch Deskpet (saved by Fritzing 0.9.9b)
breadboards: 1

parts:
  Composant1 = Arduino Nano (Rev3.0)
  OLED_I2C1 = OLED 128x64 I2C Monochrome Display
  HC-SR04_Sensor_1 = HC-SR04 Ultrasonic Distance Sensor
  J1 = Piezo Speaker

nets:
  GND: Composant1.GND, OLED_I2C1.GND, HC-SR04_Sensor_1.GND, J1.pin1
  N1: Composant1.D5, J1.pin2
  N2: Composant1.D11/MOSI, HC-SR04_Sensor_1.ECHO
  N3: Composant1.D12/MISO, HC-SR04_Sensor_1.TRIG
  5V: Composant1.5V, OLED_I2C1.VDD, HC-SR04_Sensor_1.VCC
  N4: Composant1.A5, OLED_I2C1.SCK
  N5: Composant1.A4, OLED_I2C1.SDA
